# Fritzing sketch mpr121_mmi (saved by Fritzing 0.9.3b)
breadboards: 1

parts:
  Composant1 = Adafruit MPR121
  Composant2 = Adafruit Metro Mini [part_number="Adafruit #2590"]

nets:
  GND: Composant1.GND, Composant2.GND
  VIN: Composant1.VIN, Composant2.+5V
  N1: Composant1.SDA, Composant2.AD4/SDA
  N2: Composant1.SCL, Composant2.AD5/SCL

custom parts:
  Adafruit MPR121: Add lots of touch sensors to your next microcontroller project with this easy-to-use 12-channel capacitive touch sensor breakout board, starring the MPR121. This chip can handle up to 12 individual touch pads. The MPR121 has support for only I2C, which can be implemented with nearly any microcontroller. You can select one of 4 addresses with the ADDR pin, for a total of 48 capacitive touch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
  Adafruit Metro Mini: We sure love the ATmega328 here at Adafruit, and we use them a lot for our own projects. The processor has plenty of GPIO, Analog inputs, hardware UART SPI and I2C, timers and PWM galore - just enough for most simple projects. When we need to go small, we use a Pro Trinket 3V or 5V, but if you want to have USB-to-Serial built in, we reach for an Adafruit METRO Mini. METRO Mini is the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
